# Fritzing sketch Neopixel Matrix Rail v1 (saved by Fritzing 0.9.3b)
circuit board: 21.67cm x 1.66882cm
breadboards: 1

parts:
  GND/DIN/VCC = female pin header, 3 pins [form="♀ (female)"]
  GND/DIN/VCC_2 = female pin header, 3 pins [form="♀ (female)"]
  VCC/DOUT/GND = female pin header, 3 pins [form="♀ (female)"]
  GND/DIN/VCC_3 = female pin header, 3 pins [form="♀ (female)"]
  GND/DIN/VCC_4 = female pin header, 3 pins [form="♀ (female)"]
  GND/DIN/VCC_5 = female pin header, 3 pins [form="♀ (female)"]
  GND/DIN/VCC_6 = female pin header, 3 pins [form="♀ (female)"]
  GND/DIN/VCC_7 = female pin header, 3 pins [form="♀ (female)"]
  VCC/DOUT/GND_2 = female pin header, 3 pins [form="♀ (female)"]
  VCC/DOUT/GND_3 = female pin header, 3 pins [form="♀ (female)"]
  VCC/DOUT/GND_4 = female pin header, 3 pins [form="♀ (female)"]
  VCC/DOUT/GND_5 = female pin header, 3 pins [form="♀ (female)"]
  VCC/DOUT/GND_6 = female pin header, 3 pins [form="♀ (female)"]
  GND/DIN/VCC_8 = female pin header, 3 pins [form="♀ (female)"]

nets:
  N1: GND/DIN/VCC.pin1, GND/DIN/VCC_2.pin1, VCC/DOUT/GND.pin3, GND/DIN/VCC_3.pin1, GND/DIN/VCC_4.pin1, GND/DIN/VCC_5.pin1, GND/DIN/VCC_6.pin1, GND/DIN/VCC_7.pin1, VCC/DOUT/GND_2.pin3, VCC/DOUT/GND_3.pin3, VCC/DOUT/GND_4.pin3, VCC/DOUT/GND_5.pin3, VCC/DOUT/GND_6.pin3, GND/DIN/VCC_8.pin1
  N2: GND/DIN/VCC.pin2, GND/DIN/VCC_8.pin2
  N3: GND/DIN/VCC.pin3, GND/DIN/VCC_2.pin3, VCC/DOUT/GND.pin1, GND/DIN/VCC_3.pin3, GND/DIN/VCC_4.pin3, GND/DIN/VCC_5.pin3, GND/DIN/VCC_6.pin3, GND/DIN/VCC_7.pin3, VCC/DOUT/GND_2.pin1, VCC/DOUT/GND_3.pin1, VCC/DOUT/GND_4.pin1, VCC/DOUT/GND_5.pin1, VCC/DOUT/GND_6.pin1, GND/DIN/VCC_8.pin3
  N4: GND/DIN/VCC_2.pin2, VCC/DOUT/GND.pin2
  N5: GND/DIN/VCC_3.pin2, VCC/DOUT/GND_2.pin2
  N6: GND/DIN/VCC_4.pin2, VCC/DOUT/GND_3.pin2
  N7: GND/DIN/VCC_5.pin2, VCC/DOUT/GND_4.pin2
  N8: GND/DIN/VCC_6.pin2, VCC/DOUT/GND_5.pin2
  N9: GND/DIN/VCC_7.pin2, VCC/DOUT/GND_6.pin2

notes:
  Neopixel Matrix Rail v1
