# Fritzing sketch rail-pcb-4-437a9086-6fd1-4fee-863a-2b07cfdd0b15 (saved by Fritzing 0.9.3b)
circuit board: 21.67cm x 1.66882cm
breadboards: 1

parts:
  L1 = female pin header, 3 pins [form="♀ (female)"]
  L2 = female pin header, 3 pins [form="♀ (female)"]
  L3 = female pin header, 3 pins [form="♀ (female)"]
  L4 = female pin header, 3 pins [form="♀ (female)"]
  L5 = female pin header, 3 pins [form="♀ (female)"]
  L6 = female pin header, 3 pins [form="♀ (female)"]
  L7 = female pin header, 3 pins [form="♀ (female)"]
  L8 = female pin header, 3 pins [form="♀ (female)"]
  L9 = female pin header, 3 pins [form="♀ (female)"]
  L10 = female pin header, 3 pins [form="♀ (female)"]
  L11 = female pin header, 3 pins [form="♀ (female)"]
  L12 = female pin header, 3 pins [form="♀ (female)"]
  L13 = female pin header, 3 pins [form="♀ (female)"]
  GND/DI/VCC = female pin header, 3 pins [form="♀ (female)"]
  R1 = female pin header, 3 pins [form="♀ (female)"]
  R2 = female pin header, 3 pins [form="♀ (female)"]
  R3 = female pin header, 3 pins [form="♀ (female)"]
  R4 = female pin header, 3 pins [form="♀ (female)"]
  R5 = female pin header, 3 pins [form="♀ (female)"]
  R6 = female pin header, 3 pins [form="♀ (female)"]
  R7 = female pin header, 3 pins [form="♀ (female)"]
  R8 = female pin header, 3 pins [form="♀ (female)"]
  R9 = female pin header, 3 pins [form="♀ (female)"]
  R10 = female pin header, 3 pins [form="♀ (female)"]
  R11 = female pin header, 3 pins [form="♀ (female)"]
  R12 = female pin header, 3 pins [form="♀ (female)"]
  R13 = female pin header, 3 pins [form="♀ (female)"]
  VCC/DO/GND = female pin header, 3 pins [form="♀ (female)"]

nets:
  N1: L1.pin1, L2.pin1, L3.pin1, L4.pin1, L5.pin1, L6.pin1, L7.pin1, L8.pin1, L9.pin1, L10.pin1, L11.pin1, L12.pin1, L13.pin1, GND/DI/VCC.pin1
  N2: L1.pin2, GND/DI/VCC.pin2
  N3: L1.pin3, L2.pin3, L3.pin3, L4.pin3, L5.pin3, L6.pin3, L7.pin3, L8.pin3, L9.pin3, L10.pin3, L11.pin3, L12.pin3, L13.pin3, GND/DI/VCC.pin3
  N4: L2.pin2, L3.pin2
  N5: L4.pin2, L5.pin2
  N6: L6.pin2, L7.pin2
  N7: L8.pin2, L9.pin2
  N8: L10.pin2, L11.pin2
  N9: L12.pin2, L13.pin2
  N10: R1.pin1, R2.pin1, R3.pin1, R4.pin1, R5.pin1, R6.pin1, R7.pin1, R8.pin1, R9.pin1, R10.pin1, R11.pin1, R12.pin1, R13.pin1, VCC/DO/GND.pin1
  N11: R1.pin2, R2.pin2
  N12: R1.pin3, R2.pin3, R3.pin3, R4.pin3, R5.pin3, R6.pin3, R7.pin3, R8.pin3, R9.pin3, R10.pin3, R11.pin3, R12.pin3, R13.pin3, VCC/DO/GND.pin3
  N13: R3.pin2, R4.pin2
  N14: R5.pin2, R6.pin2
  N15: R7.pin2, R8.pin2
  N16: R9.pin2, R10.pin2
  N17: R11.pin2, R12.pin2
  N18: R13.pin2, VCC/DO/GND.pin2

notes:
  Neopixel Matrix Rail v4
